// Logisim project MAC0329_EP1_Parte1.circ as structural Verilog: 4 circuits, main circuit addition_subtraction
module main (
  input  [7:0] B,
  input  [7:0] A,
  input  OP,
  output o1,
  output o2,
  output [7:0] R
);

  addition_subtraction addition_subtraction_1 (.OP(OP), .B(B), .A(A), .R(R), .o2(o2), .o1(o1));

  // Notes on the sheet:
  //   Convenção:
  //   OP: 0 -> R = A + B
  //   OP: 1 -> R = A - B
  //   Integrantes (Nome : Número USP)
  //   - Gabriel Freire Ushijima : 15453282
  //   - Renzo Real Machado Filho : 15486907
  //   - Antônio Felipe Alves Araújo : 15584024
  //   Big Endian
  //   Dígito mais significativo à esquerda.
  //   Overflow (Sem Sinal)
  //   Overflow (Complemento de 2)
endmodule

module addition_subtraction (
  input  [7:0] B,
  input  [7:0] A,
  input  OP,
  output o2,
  output [7:0] R,
  output o1
);

  wire byte_adder_1_c7, byte_adder_1_c8;
  wire [7:0] xor_1_out;

  assign xor_1_out = B ^ {8{OP}};  // XOR_Gate xor_1, 8 bits wide
  byte_adder byte_adder_1 (.A(A), .B(xor_1_out), .c0(OP), .c7(byte_adder_1_c7), .c8(byte_adder_1_c8), .S(R));
  xor xor_2 (o2, byte_adder_1_c7, byte_adder_1_c8);
  xor xor_3 (o1, byte_adder_1_c8, OP);
endmodule

module byte_adder (
  input  c0,
  input  [7:0] A,
  input  [7:0] B,
  output [7:0] S,
  output c7,
  output c8
);

  wire bit_adder_1_c_out, bit_adder_2_c_out, bit_adder_3_c_out, bit_adder_4_c_out, bit_adder_5_c_out,
       bit_adder_6_c_out;

  bit_adder bit_adder_1 (.a(A[0]), .b(B[0]), .c_in(c0), .s(S[0]), .c_out(bit_adder_1_c_out));
  bit_adder bit_adder_2 (.a(A[1]), .b(B[1]), .c_in(bit_adder_1_c_out), .s(S[1]), .c_out(bit_adder_2_c_out));
  bit_adder bit_adder_3 (.a(A[2]), .b(B[2]), .c_in(bit_adder_2_c_out), .s(S[2]), .c_out(bit_adder_3_c_out));
  bit_adder bit_adder_4 (.a(A[3]), .b(B[3]), .c_in(bit_adder_3_c_out), .s(S[3]), .c_out(bit_adder_4_c_out));
  bit_adder bit_adder_5 (.a(A[4]), .b(B[4]), .c_in(bit_adder_4_c_out), .s(S[4]), .c_out(bit_adder_5_c_out));
  bit_adder bit_adder_6 (.a(A[5]), .b(B[5]), .c_in(bit_adder_5_c_out), .s(S[5]), .c_out(bit_adder_6_c_out));
  bit_adder bit_adder_7 (.a(A[6]), .b(B[6]), .c_in(bit_adder_6_c_out), .s(S[6]), .c_out(c7));
  bit_adder bit_adder_8 (.a(A[7]), .b(B[7]), .c_in(c7), .s(S[7]), .c_out(c8));
endmodule

module bit_adder (
  input  a,
  input  b,
  input  c_in,
  output s,
  output c_out
);

  wire and_1_out, and_2_out, xor_1_out;

  xor xor_1 (xor_1_out, a, b);
  xor xor_2 (s, xor_1_out, c_in);
  and and_1 (and_1_out, xor_1_out, c_in);
  and and_2 (and_2_out, a, b);
  or or_1 (c_out, and_1_out, and_2_out);
endmodule
