// Logisim project MAC0329_EP1_Parte2.circ as structural Verilog: 10 circuits, main circuit main
module main (
  input  [7:0] B,
  input  [7:0] A,
  input  OP,
  output o1,
  output o2,
  output c0,
  output c1,
  output c2,
  output c3,
  output c4,
  output c5,
  output [7:0] R
);

  ULA ula_1 (.B(B), .A(A), .OP(OP), .R(R), .c3(c3), .c4(c4), .c5(c5), .c0(c0), .c1(c1), .c2(c2), .o1(o1), .o2(o2));

  // Notes on the sheet:
  //   Convenção:
  //   OP: 0 -> R = A + B
  //   OP: 1 -> R = A - B
  //   Big Endian
  //   Dígito mais significativo à esquerda.
  //   Integrantes (Nome : Número USP)
  //   - Gabriel Freire Ushijima : 15453282
  //   - Renzo Real Machado Filho : 15486907
  //   - Antônio Felipe Alves Araújo : 15584024
  //   Overflow (Sem Sinal)
  //   A > B (Sem Sinal)
  //   A < B (Sem Sinal)
  //   A == B
  //   A == 0
  //   Overflow (Complemento de 2)
  //   A > B (Complemento de 2)
  //   A < B (Complemento de 2)
endmodule

module ULA (
  input  [7:0] B,
  input  [7:0] A,
  input  OP,
  output c0,
  output c1,
  output c2,
  output c3,
  output c4,
  output c5,
  output o1,
  output o2,
  output [7:0] R
);

  comp comp_1 (.A(A), .B(B), .c1(c1), .c5(c5), .c2(c2), .c3(c3), .c0(c0), .c4(c4));
  addition_subtraction addition_subtraction_1 (.OP(OP), .B(B), .A(A), .R(R), .o2(o2), .o1(o1));
endmodule

module addition_subtraction (
  input  [7:0] B,
  input  [7:0] A,
  input  OP,
  output o2,
  output [7:0] R,
  output o1
);

  wire byte_adder_1_c7, byte_adder_1_c8;
  wire [7:0] xor_1_out;

  assign xor_1_out = B ^ {8{OP}};  // XOR_Gate xor_1, 8 bits wide
  byte_adder byte_adder_1 (.A(A), .B(xor_1_out), .c0(OP), .c7(byte_adder_1_c7), .c8(byte_adder_1_c8), .S(R));
  xor xor_2 (o2, byte_adder_1_c7, byte_adder_1_c8);
  xor xor_3 (o1, byte_adder_1_c8, OP);

  // Notes on the sheet:
  //   A - B = A + ~B + 1
  //   OP = 0 -> 00000000
  //   OP = 1 -> 11111111
  //   Overflow 1 (Sem Sinal)
  //   - o1 = (c8 == 1) se OP == 0
  //   - o1 = (c8 == 0) se OP == 1
  //   ≡
  //   - o1 = (OP ⊻ c8)
  //   Inverte os bits de B, se OP = 1
  //   c0 = OP
  //   ≡
  //   - o2 = (c7 ⊻ c8)
  //   Overflow 2 (Complemento de 2)
  //   - o2 = (c7 ∧ ¬c8) ∨ (¬c7 ∧ c8)
endmodule

module byte_adder (
  input  c0,
  input  [7:0] A,
  input  [7:0] B,
  output [7:0] S,
  output c7,
  output c8
);

  wire bit_adder_1_c_out, bit_adder_2_c_out, bit_adder_3_c_out, bit_adder_4_c_out, bit_adder_5_c_out,
       bit_adder_6_c_out;

  bit_adder bit_adder_1 (.b(B[0]), .c_in(c0), .a(A[0]), .s(S[0]), .c_out(bit_adder_1_c_out));
  bit_adder bit_adder_2 (.b(B[1]), .c_in(bit_adder_1_c_out), .a(A[1]), .s(S[1]), .c_out(bit_adder_2_c_out));
  bit_adder bit_adder_3 (.b(B[2]), .c_in(bit_adder_2_c_out), .a(A[2]), .s(S[2]), .c_out(bit_adder_3_c_out));
  bit_adder bit_adder_4 (.b(B[3]), .c_in(bit_adder_3_c_out), .a(A[3]), .s(S[3]), .c_out(bit_adder_4_c_out));
  bit_adder bit_adder_5 (.b(B[4]), .c_in(bit_adder_4_c_out), .a(A[4]), .s(S[4]), .c_out(bit_adder_5_c_out));
  bit_adder bit_adder_6 (.b(B[5]), .c_in(bit_adder_5_c_out), .a(A[5]), .s(S[5]), .c_out(bit_adder_6_c_out));
  bit_adder bit_adder_7 (.b(B[6]), .c_in(bit_adder_6_c_out), .a(A[6]), .s(S[6]), .c_out(c7));
  bit_adder bit_adder_8 (.b(B[7]), .c_in(c7), .a(A[7]), .s(S[7]), .c_out(c8));
endmodule

module bit_adder (
  input  a,
  input  b,
  input  c_in,
  output s,
  output c_out
);

  wire and_1_out, and_2_out, xor_1_out;

  xor xor_1 (xor_1_out, a, b);
  xor xor_2 (s, xor_1_out, c_in);
  and and_1 (and_1_out, xor_1_out, c_in);
  and and_2 (and_2_out, a, b);
  or or_1 (c_out, and_1_out, and_2_out);

  // Notes on the sheet:
  //   s = (a ⊻ b) ⊻ c_in
  //   c_out = ((a ⊻ b) ∧ c_in) ∨ (a ∧ b)
endmodule

module comp (
  input  [7:0] A,
  input  [7:0] B,
  output c0,
  output c4,
  output c1,
  output c5,
  output c2,
  output c3
);

  greater_than greater_than_1 (.B(B), .A(A), .AgtB2(c4), .AgtB1(c0));
  less_than less_than_1 (.A(A), .B(B), .AltBs(c5), .AltBu(c1));
  equals equals_1 (.B(B), .A(A), .AeqB(c2));
  equals equals_2 (.B({8{1'b0}}), .A(A), .AeqB(c3));
endmodule

module greater_than (
  input  [7:0] A,
  input  [7:0] B,
  output AgtB1,
  output AgtB2
);

  wire equals_1_aeqb, less_than_1_altbs, less_than_1_altbu, not_1_out, not_2_out, not_3_out;

  equals equals_1 (.B(B), .A(A), .AeqB(equals_1_aeqb));
  less_than less_than_1 (.A(A), .B(B), .AltBs(less_than_1_altbs), .AltBu(less_than_1_altbu));
  not not_1 (not_1_out, equals_1_aeqb);
  not not_2 (not_2_out, less_than_1_altbu);
  not not_3 (not_3_out, less_than_1_altbs);
  and and_1 (AgtB1, not_1_out, not_2_out);
  and and_2 (AgtB2, not_1_out, not_3_out);

  // Notes on the sheet:
  //   A > B ⇔ ¬ (A < B) ∧ ¬ (A == B)
endmodule

module equals (
  input  [7:0] A,
  input  [7:0] B,
  output AeqB
);

  wire less_than_1_altbu, less_than_2_altbu;

  less_than less_than_1 (.A(A), .B(B), .AltBu(less_than_1_altbu));  // open: AltBs
  less_than less_than_2 (.A(B), .B(A), .AltBu(less_than_2_altbu));  // open: AltBs
  and and_1 (AeqB, ~less_than_1_altbu, ~less_than_2_altbu);  // AND_Gate

  // Notes on the sheet:
  //   A == B ⇔ ¬ (A < B) ∧ ¬ (B < A)
endmodule

module less_than (
  input  [7:0] A,
  input  [7:0] B,
  output AltBs,
  output AltBu
);

  wire bit_comparer_1_altb, bit_comparer_1_en_out, bit_comparer_2_altb, bit_comparer_2_en_out,
       bit_comparer_3_altb, bit_comparer_3_en_out, bit_comparer_4_altb, bit_comparer_4_en_out,
       bit_comparer_5_altb, bit_comparer_5_en_out, bit_comparer_6_altb, bit_comparer_6_en_out,
       bit_comparer_7_altb, bit_comparer_7_en_out, bit_comparer_8_altb, xor_1_out;

  xor xor_1 (xor_1_out, B[7], A[7]);
  bit_comparer bit_comparer_1 (
    .b(B[7]), .en_in(1'b1), .a(A[7]), .altb(bit_comparer_1_altb), .en_out(bit_comparer_1_en_out));
  bit_comparer bit_comparer_2 (
    .b(B[6]), .en_in(bit_comparer_1_en_out), .a(A[6]), .altb(bit_comparer_2_altb),
    .en_out(bit_comparer_2_en_out));
  bit_comparer bit_comparer_3 (
    .b(B[5]), .en_in(bit_comparer_2_en_out), .a(A[5]), .altb(bit_comparer_3_altb),
    .en_out(bit_comparer_3_en_out));
  bit_comparer bit_comparer_4 (
    .b(B[4]), .en_in(bit_comparer_3_en_out), .a(A[4]), .altb(bit_comparer_4_altb),
    .en_out(bit_comparer_4_en_out));
  bit_comparer bit_comparer_5 (
    .b(B[3]), .en_in(bit_comparer_4_en_out), .a(A[3]), .altb(bit_comparer_5_altb),
    .en_out(bit_comparer_5_en_out));
  bit_comparer bit_comparer_6 (
    .b(B[2]), .en_in(bit_comparer_5_en_out), .a(A[2]), .altb(bit_comparer_6_altb),
    .en_out(bit_comparer_6_en_out));
  bit_comparer bit_comparer_7 (
    .b(B[1]), .en_in(bit_comparer_6_en_out), .a(A[1]), .altb(bit_comparer_7_altb),
    .en_out(bit_comparer_7_en_out));
  bit_comparer bit_comparer_8 (
    .b(B[0]), .en_in(bit_comparer_7_en_out), .a(A[0]), .altb(bit_comparer_8_altb));  // open: en_out
  or or_1 (AltBu, bit_comparer_1_altb, bit_comparer_2_altb, bit_comparer_3_altb, bit_comparer_4_altb, bit_comparer_5_altb, bit_comparer_6_altb, bit_comparer_7_altb, bit_comparer_8_altb);
  xor xor_2 (AltBs, xor_1_out, AltBu);

  // Notes on the sheet:
  //   se o sinal de A e B são diferentes.
  //   Inverte o resultado de A < B (Sem Sinal)
endmodule

module bit_comparer (
  input  a,
  input  b,
  input  en_in,
  output altb,
  output en_out
);

  wire xnor_1_out;

  and and_1 (altb, ~a, b, en_in);  // AND_Gate
  xnor xnor_1 (xnor_1_out, a, b);
  and and_2 (en_out, xnor_1_out, en_in);
endmodule
