// Logisim project MAC0329_EP1_Parte3.circ as structural Verilog: 12 circuits, main circuit CPU
module CPU (
  input  Reset,
  input  [7:0] Inp,
  output [7:0] Outp
);

  wire AC_we, AC_write_from, and_2_out, CLK, CLKA0, CLKA1, CLKA2, CLKA3, CLKA4, CLKB0, CLKB1, CLKB2, CLKB3,
       CLKB4, CLKB5, CLKB6, CLKB7, CLKB8, clock_1_out, decoder_1_out3, decoder_1_out5, decoder_1_out11,
       decoder_1_out12, decoder_1_out13, decoder_1_out14, Input_write_from, not_1_out, or_1_out, or_2_out,
       or_4_out, Output_write_to, PC_we, RAM_read, RAM_we, Running, Stop, ula_1_c0, ula_1_c4, ula_1_c5,
       ULA_comp_out, ULA_is_comp, ULA_op, ULA_write_from;
  wire [1:0] priority_encoder_1_out, ULA_comp_op;
  wire [7:0] AC_in, AC_out, IRee, IRii, Output_in, pc_1_outp, PC_out, RAM_addr, RAM_most, RAM_write, ULA_in,
       ULA_result;

  Clock clock_1 (.out(clock_1_out));
  not not_1 (not_1_out, Stop);
  and and_1 (CLK, clock_1_out, Running);
  two_step_clock two_step_clock_1 (
    .CLK(CLK), .Reset(Reset), .CLKA0(CLKA0), .CLKA1(CLKA1), .CLKA2(CLKA2), .CLKA3(CLKA3), .CLKA4(CLKA4),
    .CLKB0(CLKB0), .CLKB1(CLKB1), .CLKB2(CLKB2), .CLKB3(CLKB3), .CLKB4(CLKB4), .CLKB5(CLKB5), .CLKB6(CLKB6),
    .CLKB7(CLKB7), .CLKB8(CLKB8));
  D_Flip_Flop d_ff_1 (.D(not_1_out), .clk(CLKB2), .Q(Running), .preset(Reset));  // open: Qn, reset
  Register register_1 (.D(Output_in), .en(Output_write_to), .clk(CLKB8), .Q(Outp), .clr(Reset));
  PC pc_1 (.WriteClock(CLKB3), .CountCLK(CLKA3), .Inp(IRee), .InputEnable(PC_we), .Reset(Reset), .outp(pc_1_outp));
  Multiplexer #(.width(8)) multiplexer_1 (.in0(AC_out), .in1(Inp), .out(RAM_write), .sel(Input_write_from));
  Multiplexer #(.width(8)) multiplexer_2 (.in0(Output_in), .in1({8{1'b0}}), .out(ULA_in), .sel(ULA_is_comp));
  Multiplexer #(.width(8)) multiplexer_3 (.in0(PC_out), .in1(IRee), .out(RAM_addr), .sel(and_2_out));
  and and_2 (and_2_out, or_1_out, CLKB0);
  Decoder #(.select(4)) decoder_1 (
    .out1(Stop), .out3(decoder_1_out3), .out4(AC_write_from), .out5(decoder_1_out5), .out6(ULA_op),
    .out8(Input_write_from), .out9(Output_write_to), .out11(decoder_1_out11), .out12(decoder_1_out12),
    .out13(decoder_1_out13), .out14(decoder_1_out14), .sel(IRii[3:0]));  // open: out0, out2, out7, out10, out15, en
  Multiplexer #(.width(8)) multiplexer_4 (.in0(pc_1_outp), .in1(IRee), .out(PC_out), .sel(CLKB0));
  Multiplexer #(.width(8)) multiplexer_5 (.in0(Output_in), .in1(ULA_result), .out(AC_in), .sel(ULA_write_from));
  or or_1 (or_1_out, AC_write_from, Input_write_from, RAM_read);
  and and_3 (PC_we, ULA_is_comp, ULA_comp_out, CLKB0);
  ULA ula_1 (
    .B(ULA_in), .A(AC_out), .OP(ULA_op), .R(ULA_result), .c4(ula_1_c4), .c5(ula_1_c5), .c0(ula_1_c0));  // open: c3, c1, c2, o1, o2
  Multiplexer #(.select(2)) multiplexer_6 (
    .in0(1'b1), .in1(ula_1_c4), .in2(ula_1_c0), .in3(ula_1_c5), .out(ULA_comp_out), .sel(ULA_comp_op));
  RAM #(.dataWidth(16)) ram_1 (
    .addr(RAM_addr), .we(RAM_we), .oe(1'b1), .clk(or_2_out), .din({{8{1'b0}}, RAM_write}),
    .dout({RAM_most, Output_in}));
  or or_2 (or_2_out, CLKA1, CLKB2);
  or or_3 (AC_we, decoder_1_out3, decoder_1_out5, ULA_op);
  or or_4 (or_4_out, AC_write_from, Input_write_from);
  Register AC (.D(AC_in), .en(AC_we), .clk(CLKB8), .Q(AC_out), .clr(Reset));
  or or_5 (ULA_write_from, decoder_1_out5, ULA_op);
  or or_6 (RAM_read, decoder_1_out3, decoder_1_out5, decoder_1_out5);
  Priority_Encoder #(.select(2)) priority_encoder_1 (
    .in0(decoder_1_out11), .in1(decoder_1_out12), .in2(decoder_1_out13), .in3(decoder_1_out14),
    .out(priority_encoder_1_out), .gs(ULA_is_comp));  // open: en_out, en_in
  Register #(.width(16)) IR (.D({RAM_most, Output_in}), .en(CLKA2), .clk(CLKA2), .Q({IRii, IRee}), .clr(Reset));
  and and_4 (RAM_we, CLKB0, or_4_out);
  Multiplexer #(.width(2)) multiplexer_7 (
    .in0(2'b00), .in1(priority_encoder_1_out), .out(ULA_comp_op), .sel(ULA_is_comp));

  // Other names for the same wires on the sheet: PC_in[7:0] = IRee; Output_out[7:0] = Outp;
  //   RAM_least[7:0] = Output_in; RAM_out[15:0] = {RAM_most, Output_in}

  // Notes on the sheet:
  //   Convenção:
  //   Comparações para o desvio
  //   Deixe o clock rodar para a
  //   executar as instruções.
  //   O programa para sozinho
  //   em uma instrução de pare.
  //   Program Counter.
  //   Big Endian
  //   Dígito mais significativo à esquerda.
  //   seguem a notação complemento de 2.
  //   Para o programa se `Stop` vale 1.
  //   Passa o valor no IR para o PC.
  //   Passa o valor na RAM para o Output.
  //   Escreve em Output se `Output write to` vale 1.
  //   Esse valor é escrito no acumulador, se AC_we vale 1.
  //   Esse valor é escrito na RAM, se RAM_we vale 1.
  //   Preenche os bits mais significativos com 0.
  //   Esse valor é passado para a ULA, como operando.
  //   Esse valor é passado para a RAM como endereço.
  //   Para ser lido durante o passo execute (CLKB).
  //   Permite que se escreva no PC, apenas se:
  //   - CLKB0: Estamos no passo execute
  //   Para executar: 
  //   Fibonacci:
  //   Escolhe entre o valor na RAM e resultado da ULA, dependendo da intrução
  //   Escolhe entre o valor no AC e Input, dependendo da intrução
  //   Escolhe entre o valor na RAM e 0, dependendo da instrução.
  //   Escolhe entre o valor no PC e IR, dependendo da instrução.
  //   - ULA_is_comp: Estamos lidando com uma instrução de desvio.
  //   - ULA_comp_out: A condição de desvio foi bem sucedida.
  //   Seleciona o resultado da comparação de acordo com a operação.
  //   Use "Reset" para reiniciar os registradores.
  //   O valor em "Inp" será lido e colocado na RAM,
  //   quando uma instrução de leitura for executada.
  //   Um valor será escito em "Outp" quando
  //   uma instrução de escrita for executada.
  //   - Ligue e desligue o pino "Reset".
  //   - Coloque "Inp" em um valor positivo.
  //   - Deixe o Clock rodar na simulação
  //   Computa as operações entre AC_out e ULA_in, usa ULA_op como operador.
  //   - 1 -> A > 0
  //   - 2 -> A == 0
  //   - 3 -> A < 0
  //   Integrantes (Nome : Número USP):
  //   - Gabriel Freire Ushijima : 15453282
  //   Note que levam várias instruções para o resultado atualizar.
  //   Colocar o clock em 16.0Hz ou 32.0Hz pode ser apropriado
  //   Operações de Comparação:
  //   - 0 -> Icondicional (sempre 1)
  //   Para a execução.
  //   - Renzo Real Machado Filho : 15486907
  //   - Antônio Felipe Alves Araújo : 15584024
  //   As seguintes instruções computam a sequência de Fibonacci, enquanto "Inp" > 0.
  //   Acumulador.
  //   Registrador de instruções.
  //   0000 0001 0000 0000 0803 0303 0c08 0100 0900 0300 0501 0402 0301 0400 0302 0401 0b04
  //   Permite que se escreva no AC.
  //   Indica a operação da ULA.
  //   Permite que se escreva na RAM.
  //   Indica que vamos ler da RAM.
  //   Permite que se escreva no Output.
  //   Indica que vamos escrever um valor do AC na RAM.
  //   Indica que vamos escrever um valor da ULA na RAM.
  //   Indica que vamos escrever do Input.
  //   Indica a operação da comparação
  //   Indica que tentaremos um devio.
endmodule

module PC (
  input  InputEnable,
  input  [7:0] Inp,
  input  Reset,
  input  WriteClock,
  input  CountCLK,
  output [7:0] outp
);

  wire and_1_out, CLK, not_1_out, or_1_out, WE;
  wire [7:0] byte_adder_1_s, multiplexer_1_out;

  not not_1 (not_1_out, InputEnable);
  Multiplexer #(.width(8)) multiplexer_1 (.in0(Inp), .in1(byte_adder_1_s), .out(multiplexer_1_out), .sel(not_1_out));
  and and_1 (and_1_out, WriteClock, InputEnable);
  Register register_1 (.D(multiplexer_1_out), .en(WE), .clk(CLK), .Q(outp), .clr(Reset));
  or or_1 (or_1_out, WriteClock, CountCLK);
  buf buffer_1 (CLK, or_1_out);
  or or_2 (WE, CountCLK, and_1_out);
  byte_adder byte_adder_1 (.A(outp), .B(8'h1), .S(byte_adder_1_s));  // open: c0, c7, c8

  // Other names for the same wires on the sheet: InpEn = InputEnable

  // Notes on the sheet:
  //   Registra o endereço da próxima intstrução.
  //   - Count: Aumenta em 1 o valor no registrador
  //   - Input: Escreve no registrador o valor em Inp
  //   O efeito de Count só ocorre quando CountCLK sobe.
  //   O mesmo vale para Input com WriteCLK.
  //   Tem dois modos, Count e Input, marcados pelo bit InputEnable
endmodule

module two_step_clock (
  input  CLK,
  input  Reset,
  output CLKA0,
  output CLKA1,
  output CLKA2,
  output CLKA3,
  output CLKA4,
  output CLKB0,
  output CLKB1,
  output CLKB2,
  output CLKB3,
  output CLKB4,
  output CLKB5,
  output CLKB6,
  output CLKB7,
  output CLKB8
);

  wire buffer_1_out, buffer_2_out, buffer_3_out, buffer_4_out, buffer_5_out, buffer_6_out, buffer_7_out,
       buffer_8_out, buffer_9_out, buffer_10_out, buffer_11_out, buffer_12_out, buffer_13_out, buffer_14_out,
       buffer_15_out, buffer_16_out, buffer_17_out, buffer_18_out, buffer_19_out, buffer_20_out,
       buffer_21_out, buffer_22_out, buffer_23_out, buffer_24_out, buffer_25_out, buffer_26_out,
       buffer_27_out, buffer_28_out, buffer_29_out, buffer_30_out, buffer_31_out, buffer_32_out,
       buffer_33_out, buffer_34_out, buffer_35_out, buffer_36_out, buffer_37_out, buffer_38_out,
       buffer_39_out, buffer_40_out, buffer_41_out, buffer_42_out, buffer_43_out, buffer_44_out,
       buffer_45_out, buffer_46_out, buffer_47_out, buffer_48_out, buffer_49_out, buffer_50_out,
       buffer_51_out, buffer_52_out, buffer_53_out, buffer_54_out, buffer_55_out, buffer_56_out,
       buffer_57_out, buffer_58_out, buffer_59_out, buffer_60_out, buffer_61_out, buffer_62_out,
       buffer_63_out, buffer_64_out, buffer_65_out, buffer_66_out, buffer_67_out, buffer_68_out,
       buffer_69_out, buffer_70_out, buffer_71_out, buffer_72_out, buffer_73_out, buffer_74_out,
       buffer_75_out, buffer_76_out, buffer_77_out, buffer_78_out, buffer_79_out, buffer_80_out,
       buffer_81_out, buffer_82_out, buffer_83_out, buffer_84_out, buffer_85_out, buffer_86_out,
       buffer_87_out, buffer_88_out, buffer_89_out, buffer_90_out, buffer_91_out, buffer_92_out,
       buffer_93_out, buffer_94_out, buffer_95_out, buffer_96_out, buffer_97_out, buffer_98_out,
       buffer_99_out, buffer_100_out, buffer_101_out, buffer_102_out, buffer_103_out, buffer_104_out,
       buffer_106_out, buffer_107_out, buffer_108_out, buffer_110_out, buffer_111_out, buffer_112_out,
       buffer_114_out, buffer_115_out, buffer_116_out, buffer_118_out, buffer_119_out, buffer_120_out,
       buffer_122_out, buffer_123_out, buffer_124_out, buffer_126_out, buffer_127_out, buffer_128_out,
       buffer_130_out, buffer_131_out, buffer_132_out, buffer_134_out, buffer_135_out, buffer_136_out,
       buffer_138_out, buffer_139_out, buffer_140_out, buffer_142_out, buffer_143_out, buffer_144_out,
       buffer_146_out, buffer_147_out, buffer_148_out, t_ff_1_q, t_ff_1_qn;

  T_Flip_Flop t_ff_1 (.T(1'b1), .clk(CLK), .Q(t_ff_1_q), .Qn(t_ff_1_qn), .reset(Reset));  // open: preset
  buf buffer_1 (buffer_1_out, CLK);
  buf buffer_2 (buffer_2_out, buffer_1_out);
  buf buffer_3 (buffer_3_out, buffer_2_out);
  buf buffer_4 (buffer_4_out, buffer_3_out);
  buf buffer_5 (buffer_5_out, CLKA0);
  buf buffer_6 (buffer_6_out, buffer_5_out);
  buf buffer_7 (buffer_7_out, buffer_6_out);
  buf buffer_8 (buffer_8_out, buffer_7_out);
  buf buffer_9 (buffer_9_out, CLKA1);
  buf buffer_10 (buffer_10_out, buffer_9_out);
  buf buffer_11 (buffer_11_out, buffer_10_out);
  buf buffer_12 (buffer_12_out, buffer_11_out);
  buf buffer_13 (buffer_13_out, CLKA2);
  buf buffer_14 (buffer_14_out, buffer_13_out);
  buf buffer_15 (buffer_15_out, buffer_14_out);
  buf buffer_16 (buffer_16_out, buffer_15_out);
  buf buffer_17 (buffer_17_out, CLKA3);
  buf buffer_18 (buffer_18_out, buffer_17_out);
  buf buffer_19 (buffer_19_out, buffer_18_out);
  buf buffer_20 (buffer_20_out, buffer_19_out);
  buf buffer_21 (buffer_21_out, CLKB0);
  buf buffer_22 (buffer_22_out, buffer_21_out);
  buf buffer_23 (buffer_23_out, buffer_22_out);
  buf buffer_24 (buffer_24_out, buffer_23_out);
  buf buffer_25 (buffer_25_out, CLKB1);
  buf buffer_26 (buffer_26_out, buffer_25_out);
  buf buffer_27 (buffer_27_out, buffer_26_out);
  buf buffer_28 (buffer_28_out, buffer_27_out);
  buf buffer_29 (buffer_29_out, CLKB2);
  buf buffer_30 (buffer_30_out, buffer_29_out);
  buf buffer_31 (buffer_31_out, buffer_30_out);
  buf buffer_32 (buffer_32_out, buffer_31_out);
  buf buffer_33 (buffer_33_out, CLKB3);
  buf buffer_34 (buffer_34_out, buffer_33_out);
  buf buffer_35 (buffer_35_out, buffer_34_out);
  buf buffer_36 (buffer_36_out, buffer_35_out);
  buf buffer_37 (buffer_37_out, CLKB4);
  buf buffer_38 (buffer_38_out, buffer_37_out);
  buf buffer_39 (buffer_39_out, buffer_38_out);
  buf buffer_40 (buffer_40_out, buffer_39_out);
  buf buffer_41 (buffer_41_out, CLKB5);
  buf buffer_42 (buffer_42_out, buffer_41_out);
  buf buffer_43 (buffer_43_out, buffer_42_out);
  buf buffer_44 (buffer_44_out, buffer_43_out);
  buf buffer_45 (buffer_45_out, CLKB6);
  buf buffer_46 (buffer_46_out, buffer_45_out);
  buf buffer_47 (buffer_47_out, buffer_46_out);
  buf buffer_48 (buffer_48_out, buffer_47_out);
  buf buffer_49 (buffer_49_out, CLKB7);
  buf buffer_50 (buffer_50_out, buffer_49_out);
  buf buffer_51 (buffer_51_out, buffer_50_out);
  buf buffer_52 (buffer_52_out, buffer_51_out);
  and and_1 (CLKB0, t_ff_1_qn, buffer_53_out);
  and and_2 (CLKA0, t_ff_1_q, buffer_53_out);
  buf buffer_53 (buffer_53_out, buffer_4_out);
  buf buffer_54 (buffer_54_out, buffer_8_out);
  buf buffer_55 (buffer_55_out, buffer_54_out);
  buf buffer_56 (buffer_56_out, buffer_55_out);
  buf buffer_57 (buffer_57_out, buffer_56_out);
  buf buffer_58 (buffer_58_out, buffer_12_out);
  buf buffer_59 (buffer_59_out, buffer_58_out);
  buf buffer_60 (buffer_60_out, buffer_59_out);
  buf buffer_61 (buffer_61_out, buffer_60_out);
  buf buffer_62 (buffer_62_out, buffer_16_out);
  buf buffer_63 (buffer_63_out, buffer_62_out);
  buf buffer_64 (buffer_64_out, buffer_63_out);
  buf buffer_65 (buffer_65_out, buffer_64_out);
  buf buffer_66 (buffer_66_out, buffer_20_out);
  buf buffer_67 (buffer_67_out, buffer_66_out);
  buf buffer_68 (buffer_68_out, buffer_67_out);
  buf buffer_69 (buffer_69_out, buffer_68_out);
  buf buffer_70 (buffer_70_out, buffer_24_out);
  buf buffer_71 (buffer_71_out, buffer_70_out);
  buf buffer_72 (buffer_72_out, buffer_71_out);
  buf buffer_73 (buffer_73_out, buffer_72_out);
  buf buffer_74 (buffer_74_out, buffer_28_out);
  buf buffer_75 (buffer_75_out, buffer_74_out);
  buf buffer_76 (buffer_76_out, buffer_75_out);
  buf buffer_77 (buffer_77_out, buffer_76_out);
  buf buffer_78 (buffer_78_out, buffer_32_out);
  buf buffer_79 (buffer_79_out, buffer_78_out);
  buf buffer_80 (buffer_80_out, buffer_79_out);
  buf buffer_81 (buffer_81_out, buffer_80_out);
  buf buffer_82 (buffer_82_out, buffer_36_out);
  buf buffer_83 (buffer_83_out, buffer_82_out);
  buf buffer_84 (buffer_84_out, buffer_83_out);
  buf buffer_85 (buffer_85_out, buffer_84_out);
  buf buffer_86 (buffer_86_out, buffer_40_out);
  buf buffer_87 (buffer_87_out, buffer_86_out);
  buf buffer_88 (buffer_88_out, buffer_87_out);
  buf buffer_89 (buffer_89_out, buffer_88_out);
  buf buffer_90 (buffer_90_out, buffer_44_out);
  buf buffer_91 (buffer_91_out, buffer_90_out);
  buf buffer_92 (buffer_92_out, buffer_91_out);
  buf buffer_93 (buffer_93_out, buffer_92_out);
  buf buffer_94 (buffer_94_out, buffer_48_out);
  buf buffer_95 (buffer_95_out, buffer_94_out);
  buf buffer_96 (buffer_96_out, buffer_95_out);
  buf buffer_97 (buffer_97_out, buffer_96_out);
  buf buffer_98 (buffer_98_out, buffer_52_out);
  buf buffer_99 (buffer_99_out, buffer_98_out);
  buf buffer_100 (buffer_100_out, buffer_99_out);
  buf buffer_101 (buffer_101_out, buffer_100_out);
  buf buffer_102 (buffer_102_out, buffer_57_out);
  buf buffer_103 (buffer_103_out, buffer_102_out);
  buf buffer_104 (buffer_104_out, buffer_103_out);
  buf buffer_105 (CLKA1, buffer_104_out);
  buf buffer_106 (buffer_106_out, buffer_61_out);
  buf buffer_107 (buffer_107_out, buffer_106_out);
  buf buffer_108 (buffer_108_out, buffer_107_out);
  buf buffer_109 (CLKA2, buffer_108_out);
  buf buffer_110 (buffer_110_out, buffer_65_out);
  buf buffer_111 (buffer_111_out, buffer_110_out);
  buf buffer_112 (buffer_112_out, buffer_111_out);
  buf buffer_113 (CLKA3, buffer_112_out);
  buf buffer_114 (buffer_114_out, buffer_69_out);
  buf buffer_115 (buffer_115_out, buffer_114_out);
  buf buffer_116 (buffer_116_out, buffer_115_out);
  buf buffer_117 (CLKA4, buffer_116_out);
  buf buffer_118 (buffer_118_out, buffer_73_out);
  buf buffer_119 (buffer_119_out, buffer_118_out);
  buf buffer_120 (buffer_120_out, buffer_119_out);
  buf buffer_121 (CLKB1, buffer_120_out);
  buf buffer_122 (buffer_122_out, buffer_77_out);
  buf buffer_123 (buffer_123_out, buffer_122_out);
  buf buffer_124 (buffer_124_out, buffer_123_out);
  buf buffer_125 (CLKB2, buffer_124_out);
  buf buffer_126 (buffer_126_out, buffer_81_out);
  buf buffer_127 (buffer_127_out, buffer_126_out);
  buf buffer_128 (buffer_128_out, buffer_127_out);
  buf buffer_129 (CLKB3, buffer_128_out);
  buf buffer_130 (buffer_130_out, buffer_85_out);
  buf buffer_131 (buffer_131_out, buffer_130_out);
  buf buffer_132 (buffer_132_out, buffer_131_out);
  buf buffer_133 (CLKB4, buffer_132_out);
  buf buffer_134 (buffer_134_out, buffer_89_out);
  buf buffer_135 (buffer_135_out, buffer_134_out);
  buf buffer_136 (buffer_136_out, buffer_135_out);
  buf buffer_137 (CLKB5, buffer_136_out);
  buf buffer_138 (buffer_138_out, buffer_93_out);
  buf buffer_139 (buffer_139_out, buffer_138_out);
  buf buffer_140 (buffer_140_out, buffer_139_out);
  buf buffer_141 (CLKB6, buffer_140_out);
  buf buffer_142 (buffer_142_out, buffer_97_out);
  buf buffer_143 (buffer_143_out, buffer_142_out);
  buf buffer_144 (buffer_144_out, buffer_143_out);
  buf buffer_145 (CLKB7, buffer_144_out);
  buf buffer_146 (buffer_146_out, buffer_101_out);
  buf buffer_147 (buffer_147_out, buffer_146_out);
  buf buffer_148 (buffer_148_out, buffer_147_out);
  buf buffer_149 (CLKB8, buffer_148_out);

  // Other names for the same wires on the sheet: CLKA = CLKA0; CLKB = CLKB0

  // Notes on the sheet:
  //   Separa um tick de clock em dois ticks principais (A e B)
  //   Ordem de subida (qual clock sobe primeiro):
  //   - CLKA0 -> ... -> CLKA4 -> CLKB0 -> ... CLKB8
  //   Cada tick tem subticks, todo subtick ocorre antes do próximo tick.
  //   Todo tick com um número maior sobe depois de um número menor
  //   Isso ajuda a garantir que as subidas de clock occorrem na ordem correta na CPU.
  //   Por exemplo, o endereço passado para a RAM é atualizado antes de seu clock subir.
endmodule

module ULA (
  input  [7:0] B,
  input  [7:0] A,
  input  OP,
  output c0,
  output c1,
  output c2,
  output c3,
  output c4,
  output c5,
  output o1,
  output o2,
  output [7:0] R
);

  comp comp_1 (.A(A), .B(B), .c3(c3), .c5(c5), .c1(c1), .c0(c0), .c2(c2), .c4(c4));
  addition_subtraction addition_subtraction_1 (.OP(OP), .B(B), .A(A), .R(R), .o2(o2), .o1(o1));

  // Notes on the sheet:
  //   OP: 0 -> R = A + B
  //   OP: 1 -> R = A - B
  //   A == 0
  //   A == B
  //   A > B (Sem Sinal)
  //   A < B (Sem Sinal)
  //   A > B (Complemento de 2)
  //   A < B (Complemento de 2)
  //   Overflow (Sem Sinal)
  //   Overflow (Complemento de 2)
endmodule

module addition_subtraction (
  input  [7:0] B,
  input  [7:0] A,
  input  OP,
  output o2,
  output [7:0] R,
  output o1
);

  wire byte_adder_1_c7, byte_adder_1_c8;
  wire [7:0] xor_1_out;

  assign xor_1_out = B ^ {8{OP}};  // XOR_Gate xor_1, 8 bits wide
  byte_adder byte_adder_1 (.A(A), .B(xor_1_out), .c0(OP), .c7(byte_adder_1_c7), .c8(byte_adder_1_c8), .S(R));
  xor xor_2 (o2, byte_adder_1_c7, byte_adder_1_c8);
  xor xor_3 (o1, byte_adder_1_c8, OP);

  // Notes on the sheet:
  //   A - B = A + ~B + 1
  //   OP = 0 -> 00000000
  //   OP = 1 -> 11111111
  //   Overflow 1 (Sem Sinal)
  //   - o1 = (c8 == 1) se OP == 0
  //   - o1 = (c8 == 0) se OP == 1
  //   ≡
  //   - o1 = (OP ⊻ c8)
  //   Inverte os bits de B, se OP = 1
  //   c0 = OP
  //   ≡
  //   - o2 = (c7 ⊻ c8)
  //   Overflow 2 (Complemento de 2)
  //   - o2 = (c7 ∧ ¬c8) ∨ (¬c7 ∧ c8)
endmodule

module byte_adder (
  input  c0,
  input  [7:0] A,
  input  [7:0] B,
  output [7:0] S,
  output c7,
  output c8
);

  wire bit_adder_1_c_out, bit_adder_2_c_out, bit_adder_3_c_out, bit_adder_4_c_out, bit_adder_5_c_out,
       bit_adder_6_c_out;

  bit_adder bit_adder_1 (.b(B[0]), .c_in(c0), .a(A[0]), .s(S[0]), .c_out(bit_adder_1_c_out));
  bit_adder bit_adder_2 (.b(B[1]), .c_in(bit_adder_1_c_out), .a(A[1]), .s(S[1]), .c_out(bit_adder_2_c_out));
  bit_adder bit_adder_3 (.b(B[2]), .c_in(bit_adder_2_c_out), .a(A[2]), .s(S[2]), .c_out(bit_adder_3_c_out));
  bit_adder bit_adder_4 (.b(B[3]), .c_in(bit_adder_3_c_out), .a(A[3]), .s(S[3]), .c_out(bit_adder_4_c_out));
  bit_adder bit_adder_5 (.b(B[4]), .c_in(bit_adder_4_c_out), .a(A[4]), .s(S[4]), .c_out(bit_adder_5_c_out));
  bit_adder bit_adder_6 (.b(B[5]), .c_in(bit_adder_5_c_out), .a(A[5]), .s(S[5]), .c_out(bit_adder_6_c_out));
  bit_adder bit_adder_7 (.b(B[6]), .c_in(bit_adder_6_c_out), .a(A[6]), .s(S[6]), .c_out(c7));
  bit_adder bit_adder_8 (.b(B[7]), .c_in(c7), .a(A[7]), .s(S[7]), .c_out(c8));
endmodule

module bit_adder (
  input  a,
  input  b,
  input  c_in,
  output s,
  output c_out
);

  wire and_1_out, and_2_out, xor_1_out;

  xor xor_1 (xor_1_out, a, b);
  xor xor_2 (s, xor_1_out, c_in);
  and and_1 (and_1_out, xor_1_out, c_in);
  and and_2 (and_2_out, a, b);
  or or_1 (c_out, and_1_out, and_2_out);

  // Notes on the sheet:
  //   s = (a ⊻ b) ⊻ c_in
  //   c_out = ((a ⊻ b) ∧ c_in) ∨ (a ∧ b)
endmodule

module comp (
  input  [7:0] A,
  input  [7:0] B,
  output c2,
  output c4,
  output c3,
  output c5,
  output c1,
  output c0
);

  greater_than greater_than_1 (.B(B), .A(A), .AgtBs(c4), .AgtBu(c2));
  less_than less_than_1 (.A(A), .B(B), .AltBs(c5), .AltBu(c3));
  equals equals_1 (.B(B), .A(A), .AeqB(c1));
  equals equals_2 (.B({8{1'b0}}), .A(A), .AeqB(c0));
endmodule

module greater_than (
  input  [7:0] A,
  input  [7:0] B,
  output AgtBu,
  output AgtBs
);

  wire equals_1_aeqb, less_than_1_altbs, less_than_1_altbu, not_1_out, not_2_out, not_3_out;

  equals equals_1 (.B(B), .A(A), .AeqB(equals_1_aeqb));
  less_than less_than_1 (.A(A), .B(B), .AltBs(less_than_1_altbs), .AltBu(less_than_1_altbu));
  not not_1 (not_1_out, equals_1_aeqb);
  not not_2 (not_2_out, less_than_1_altbu);
  not not_3 (not_3_out, less_than_1_altbs);
  and and_1 (AgtBu, not_1_out, not_2_out);
  and and_2 (AgtBs, not_1_out, not_3_out);

  // Notes on the sheet:
  //   A > B ⇔ ¬ (A < B) ∧ ¬ (A == B)
  //   A greater than B (unsigned)
  //   A greater than B (signed)
endmodule

module equals (
  input  [7:0] A,
  input  [7:0] B,
  output AeqB
);

  wire less_than_1_altbu, less_than_2_altbu;

  less_than less_than_1 (.A(A), .B(B), .AltBu(less_than_1_altbu));  // open: AltBs
  less_than less_than_2 (.A(B), .B(A), .AltBu(less_than_2_altbu));  // open: AltBs
  and and_1 (AeqB, ~less_than_1_altbu, ~less_than_2_altbu);  // AND_Gate

  // Notes on the sheet:
  //   A == B ⇔ ¬ (A < B) ∧ ¬ (B < A)
  //   A equals B
endmodule

module less_than (
  input  [7:0] A,
  input  [7:0] B,
  output AltBs,
  output AltBu
);

  wire bit_comparer_1_altb, bit_comparer_1_en_out, bit_comparer_2_altb, bit_comparer_2_en_out,
       bit_comparer_3_altb, bit_comparer_3_en_out, bit_comparer_4_altb, bit_comparer_4_en_out,
       bit_comparer_5_altb, bit_comparer_5_en_out, bit_comparer_6_altb, bit_comparer_6_en_out,
       bit_comparer_7_altb, bit_comparer_7_en_out, bit_comparer_8_altb, xor_1_out;

  xor xor_1 (xor_1_out, B[7], A[7]);
  bit_comparer bit_comparer_1 (
    .b(B[7]), .en_in(1'b1), .a(A[7]), .altb(bit_comparer_1_altb), .en_out(bit_comparer_1_en_out));
  bit_comparer bit_comparer_2 (
    .b(B[6]), .en_in(bit_comparer_1_en_out), .a(A[6]), .altb(bit_comparer_2_altb),
    .en_out(bit_comparer_2_en_out));
  bit_comparer bit_comparer_3 (
    .b(B[5]), .en_in(bit_comparer_2_en_out), .a(A[5]), .altb(bit_comparer_3_altb),
    .en_out(bit_comparer_3_en_out));
  bit_comparer bit_comparer_4 (
    .b(B[4]), .en_in(bit_comparer_3_en_out), .a(A[4]), .altb(bit_comparer_4_altb),
    .en_out(bit_comparer_4_en_out));
  bit_comparer bit_comparer_5 (
    .b(B[3]), .en_in(bit_comparer_4_en_out), .a(A[3]), .altb(bit_comparer_5_altb),
    .en_out(bit_comparer_5_en_out));
  bit_comparer bit_comparer_6 (
    .b(B[2]), .en_in(bit_comparer_5_en_out), .a(A[2]), .altb(bit_comparer_6_altb),
    .en_out(bit_comparer_6_en_out));
  bit_comparer bit_comparer_7 (
    .b(B[1]), .en_in(bit_comparer_6_en_out), .a(A[1]), .altb(bit_comparer_7_altb),
    .en_out(bit_comparer_7_en_out));
  bit_comparer bit_comparer_8 (
    .b(B[0]), .en_in(bit_comparer_7_en_out), .a(A[0]), .altb(bit_comparer_8_altb));  // open: en_out
  or or_1 (AltBu, bit_comparer_1_altb, bit_comparer_2_altb, bit_comparer_3_altb, bit_comparer_4_altb, bit_comparer_5_altb, bit_comparer_6_altb, bit_comparer_7_altb, bit_comparer_8_altb);
  xor xor_2 (AltBs, xor_1_out, AltBu);

  // Notes on the sheet:
  //   sign(A) == sign(B):
  //   sign(A) != sign(B):
  //   se o sinal de A e B são diferentes.
  //   - A < B (Com Sinal) == A < B (Sem Sinal)
  //   - A < B (Com Sinal) == ¬ (A < B (Sem Sinal))
  //   Inverte o resultado de A < B (Sem Sinal)
  //   A less than B (signed)
  //   A less than B (unsigned)
endmodule

module bit_comparer (
  input  a,
  input  b,
  input  en_in,
  output altb,
  output en_out
);

  wire xnor_1_out;

  and and_1 (altb, ~a, b, en_in);  // AND_Gate
  xnor xnor_1 (xnor_1_out, a, b);
  and and_2 (en_out, xnor_1_out, en_in);

  // Notes on the sheet:
  //   Ambos resultados são 0 se en_in == 0
  //   A verificação para se os bits de a e b são diferentes ou en_in == 0
  //   a < b ⇔ ¬a ∧ b ∧ en_in
  //   en_out ⇔ (a ⊻ b) ∧ en_in
endmodule
